# Fritzing sketch rgb_led_schema (saved by Fritzing 0.9.3b)
breadboards: 1

parts:
  Componente1 = Arduino Uno (Rev3)
  R1 = Resistor [tolerance=±5% resistance=220 package=THT]
  R2 = Resistor [tolerance=±5% resistance=220 package=THT]
  LED1 = RGB LED - (4 legs) [package="5 mm [THT]"]
  R3 = Resistor [tolerance=±5% resistance=220 package=THT]

nets:
  N1: Componente1.D9_PWM, R1.Pin_1
  N2: Componente1.D10_PWM/SS, R3.Pin_1
  N3: Componente1.D11_PWM/MOSI, R2.Pin_1
  N4: Componente1.GND, LED1.common_anode
  N5: R1.Pin_0, LED1.red_cathode
  N6: R2.Pin_0, LED1.blue_cathode
  N7: LED1.green_cathode, R3.Pin_0
