# Fritzing sketch blink_led (saved by Fritzing 0.9.3b)
circuit board: 8.46667cm x 5.64444cm
breadboards: 1

parts:
  Componente1 = Arduino Uno (Rev3)
  LED1 = LED - 5mm [color="Yellow (592nm)" package="5 mm [THT]"]
  R1 = Resistor [tolerance=±5% resistance=1k package="2512 [SMD]"]

nets:
  N1: Componente1.GND, LED1.cathode
  N2: Componente1.D2, R1.Pin_1
  N3: LED1.anode, R1.Pin_0
